// Digital circuit Banco_de_registradores.dig as structural Verilog
module Banco_de_registradores (
  input  clock,
  input  enable,
  input  [1:0] clk,
  input  [31:0] Data,
  input  [1:0] reg_a,
  input  [1:0] reg_b,
  output [31:0] S_a,
  output [31:0] S_b
);

  wire and_1_out, and_2_out, and_3_out, and_4_out, demultiplexer_1_out_0, demultiplexer_1_out_1,
       demultiplexer_1_out_2, demultiplexer_1_out_3;
  wire [31:0] register_1_q, register_2_q, register_3_q, register_4_q;

  Demultiplexer #(.Selector_Bits(2)) demultiplexer_1 (
    .sel(clk), .in(1'b1), .out_0(demultiplexer_1_out_0), .out_1(demultiplexer_1_out_1),
    .out_2(demultiplexer_1_out_2), .out_3(demultiplexer_1_out_3));
  and and_1 (and_1_out, demultiplexer_1_out_0, enable);
  and and_2 (and_2_out, demultiplexer_1_out_1, enable);
  and and_3 (and_3_out, demultiplexer_1_out_2, enable);
  and and_4 (and_4_out, demultiplexer_1_out_3, enable);
  Register #(.Bits(32)) register_1 (.D(Data), .C(clock), .en(and_1_out), .Q(register_1_q));
  Register #(.Bits(32)) register_2 (.D(Data), .C(clock), .en(and_2_out), .Q(register_2_q));
  Register #(.Bits(32)) register_3 (.D(Data), .C(clock), .en(and_3_out), .Q(register_3_q));
  Register #(.Bits(32)) register_4 (.D(Data), .C(clock), .en(and_4_out), .Q(register_4_q));
  Multiplexer #(.Bits(32), .Selector_Bits(2)) multiplexer_1 (
    .sel(reg_a), .in_0(register_1_q), .in_1(register_2_q), .in_2(register_3_q), .in_3(register_4_q), .out(S_a));
  Multiplexer #(.Bits(32), .Selector_Bits(2)) multiplexer_2 (
    .sel(reg_b), .in_0(register_1_q), .in_1(register_2_q), .in_2(register_3_q), .in_3(register_4_q), .out(S_b));
endmodule
