// Logisim project Celula Ula.circ as structural Verilog: 1 circuit, main circuit main
module main (
  input  vem_1,
  input  A,
  input  B,
  input  [4:0] in_4,
  output out_5,
  output Vai_1
);

  wire adder_1_cout, adder_1_out, and_1_out, and_2_out, comparator_1_eq, comparator_1_gt, comparator_1_lt,
       comparator_2_eq, comparator_2_gt, comparator_2_lt, not_1_out, or_1_out, shifter_1_out, shifter_2_out,
       shifter_3_out, subtractor_1_bout, subtractor_1_out, xor_1_out;

  Adder #(.width(1)) adder_1 (.a(A), .b(B), .out(adder_1_out), .cin(vem_1), .cout(adder_1_cout));
  Subtractor #(.width(1)) subtractor_1 (.a(A), .b(B), .out(subtractor_1_out), .bin(vem_1), .bout(subtractor_1_bout));
  and and_1 (and_1_out, A, B);
  or or_1 (or_1_out, A, B);
  Shifter #(.width(1)) shifter_1 (.in(A), .\dist (B), .out(shifter_1_out));
  Shifter #(.width(1), .shift("lr")) shifter_2 (.in(A), .\dist (B), .out(shifter_2_out));
  Shifter #(.width(1), .shift("ar")) shifter_3 (.in(A), .\dist (B), .out(shifter_3_out));
  Comparator #(.width(1)) comparator_1 (.a(A), .b(B), .gt(comparator_1_gt), .eq(comparator_1_eq), .lt(comparator_1_lt));
  Comparator #(.width(1), .mode("unsigned")) comparator_2 (
    .a(A), .b(B), .gt(comparator_2_gt), .eq(comparator_2_eq), .lt(comparator_2_lt));
  xor xor_1 (xor_1_out, A, B);
  not not_1 (not_1_out, comparator_2_eq);
  and and_2 (and_2_out, ~in_4[4], ~in_4[3], in_4[2], in_4[1], ~in_4[0]);  // AND_Gate
  Multiplexer #(.select(5), .enable("false")) multiplexer_1 (
    .in0(adder_1_out), .in1(subtractor_1_out), .in2(and_1_out), .in3(or_1_out), .in4(xor_1_out),
    .in5(shifter_1_out), .in6(shifter_2_out), .in7(shifter_3_out), .in8(comparator_1_gt),
    .in9(comparator_2_gt), .in10(comparator_1_lt), .in11(comparator_2_lt), .in12(comparator_1_eq),
    .in13(not_1_out), .out(out_5), .sel(in_4));  // open: in14, in15, in16, in17, in18, in19, in20, in21, in22, in23, in24, in25, in26, in27, in28, in29, in30, in31
  Multiplexer #(.enable("false")) multiplexer_2 (
    .in0(adder_1_cout), .in1(subtractor_1_bout), .out(Vai_1), .sel(and_2_out));
endmodule
