// Digital circuit Demux.dig as structural Verilog
module Demux (
  input  C0,
  input  C1,
  input  Entrada,
  output S1,
  output S2,
  output S3,
  output S4
);

  wire not_1_out, not_2_out;

  not not_1 (not_1_out, C0);
  not not_2 (not_2_out, C1);
  and and_1 (S1, not_1_out, not_2_out, Entrada);
  and and_2 (S2, C0, not_2_out, Entrada);
  and and_3 (S3, not_1_out, C1, Entrada);
  and and_4 (S4, C0, C1, Entrada);
endmodule
