// Digital circuit Flip-Flop D.dig as structural Verilog
module Flip_Flop_D (
  input  in_2,
  input  clk,
  input  in_5,
  input  in_6,
  output out_1,
  output out_3
);

  wire nand_1_out, nand_2_out, not_1_out;

  not not_1 (not_1_out, in_2);
  nand nand_1 (nand_1_out, in_2, clk, out_3);
  nand nand_2 (nand_2_out, out_1, clk, not_1_out);
  nand nand_3 (out_1, in_5, out_3);
  nand nand_4 (out_3, out_1, in_6);
endmodule
