// Digital circuit Flip-Flop Jk.dig as structural Verilog
module Flip_Flop_Jk (
  input  in_2,
  input  in_4,
  input  clk,
  input  in_6,
  input  in_7,
  input  in_8,
  input  clk_2,
  input  in_10,
  output out_1,
  output out_3,
  output out_11,
  output out_12
);

  wire nand_1_out, nand_2_out;

  JK_FF jk_ff_1 (.J(in_8), .C(clk_2), .K(in_10), .Q(out_11), .nQ(out_12));
  nand nand_1 (nand_1_out, in_2, clk, out_3);
  nand nand_2 (nand_2_out, out_1, clk, in_4);
  nand nand_3 (out_1, in_6, out_3);
  nand nand_4 (out_3, out_1, in_7);
endmodule
