// Digital circuit Flip-Flop RS Basico.dig as structural Verilog
module Flip_Flop_RS_Basico (
  input  in_2,
  input  in_4,
  output out_1,
  output out_3
);

  wire not_1_out, not_2_out;

  not not_1 (not_1_out, in_2);
  not not_2 (not_2_out, in_4);
  nand nand_1 (out_1, not_1_out, out_3);
  nand nand_2 (out_3, out_1, not_2_out);
endmodule
