// Digital circuit Flip-Flop RS Clock.dig as structural Verilog
module Flip_Flop_RS_Clock (
  input  clk,
  input  in_4,
  input  in_5,
  input  in_6,
  input  in_7,
  input  in_8,
  input  clk_2,
  input  in_10,
  output out_1,
  output out_2,
  output out_11,
  output out_12
);

  wire nand_1_out, nor_1_out;

  nor nor_1 (nor_1_out, in_4, clk, out_2);
  nand nand_1 (nand_1_out, out_1, clk, in_5);
  nand nand_2 (out_1, in_7, nor_1_out, out_2);
  nand nand_3 (out_2, out_1, nand_1_out, in_6);
  JK_FF jk_ff_1 (.J(in_8), .C(clk_2), .K(in_10), .Q(out_11), .nQ(out_12));
endmodule
