// Digital circuit Multiplexador.dig as structural Verilog
module Multiplexador (
  input  A,
  input  B,
  output Saida
);

  wire and_1_out, and_2_out, and_3_out, and_4_out;

  and and_1 (and_1_out, A, B);
  and and_2 (and_2_out, A, B);
  and and_3 (and_3_out, A, B);
  and and_4 (and_4_out, A, B);
  or or_1 (Saida, and_1_out, and_2_out, and_3_out, and_4_out);
endmodule
