// Logisim project Overflow Fora.circ as structural Verilog: 4 circuits, main circuit Overflow Fora
module main (
  input  vem_1,
  input  A,
  input  B,
  input  [4:0] in_4,
  output S,
  output Vai_1
);

  wire adder_1_cout, adder_1_out, and_1_out, and_2_out, comparator_1_eq, comparator_1_gt, comparator_1_lt,
       comparator_2_eq, comparator_2_gt, comparator_2_lt, not_1_out, or_1_out, shifter_1_out, shifter_2_out,
       shifter_3_out, subtractor_1_bout, subtractor_1_out, xor_1_out;

  Adder #(.width(1)) adder_1 (.a(A), .b(B), .out(adder_1_out), .cin(vem_1), .cout(adder_1_cout));
  Subtractor #(.width(1)) subtractor_1 (.a(A), .b(B), .out(subtractor_1_out), .bin(vem_1), .bout(subtractor_1_bout));
  and and_1 (and_1_out, A, B);
  or or_1 (or_1_out, A, B);
  Shifter #(.width(1)) shifter_1 (.in(A), .\dist (B), .out(shifter_1_out));
  Shifter #(.width(1), .shift("lr")) shifter_2 (.in(A), .\dist (B), .out(shifter_2_out));
  Shifter #(.width(1), .shift("ar")) shifter_3 (.in(A), .\dist (B), .out(shifter_3_out));
  Comparator #(.width(1)) comparator_1 (.a(A), .b(B), .gt(comparator_1_gt), .eq(comparator_1_eq), .lt(comparator_1_lt));
  Comparator #(.width(1), .mode("unsigned")) comparator_2 (
    .a(A), .b(B), .gt(comparator_2_gt), .eq(comparator_2_eq), .lt(comparator_2_lt));
  xor xor_1 (xor_1_out, A, B);
  not not_1 (not_1_out, comparator_2_eq);
  and and_2 (and_2_out, ~in_4[4], ~in_4[3], in_4[2], in_4[1], ~in_4[0]);  // AND_Gate
  Multiplexer #(.select(5), .enable("false")) multiplexer_1 (
    .in0(adder_1_out), .in1(subtractor_1_out), .in2(and_1_out), .in3(or_1_out), .in4(xor_1_out),
    .in5(shifter_1_out), .in6(shifter_2_out), .in7(shifter_3_out), .in8(comparator_1_gt),
    .in9(comparator_2_gt), .in10(comparator_1_lt), .in11(comparator_2_lt), .in12(comparator_1_eq),
    .in13(not_1_out), .out(S), .sel(in_4));  // open: in14, in15, in16, in17, in18, in19, in20, in21, in22, in23, in24, in25, in26, in27, in28, in29, in30, in31
  Multiplexer #(.enable("false")) multiplexer_2 (
    .in0(adder_1_cout), .in1(subtractor_1_bout), .out(Vai_1), .sel(and_2_out));
endmodule

module ULA (
  input  [31:0] A,
  input  [4:0] in_2,
  input  [31:0] B,
  input  [31:0] S,
  output out_5,
  output Zero
);

  wire and_1_out, main_1_vai_1, main_2_vai_1, main_3_vai_1, main_4_vai_1, main_5_vai_1, main_6_vai_1,
       main_7_vai_1, main_8_vai_1, main_9_vai_1, main_10_vai_1, main_11_vai_1, main_12_vai_1, main_13_vai_1,
       main_14_vai_1, main_15_vai_1, main_17_vai_1, main_18_vai_1, main_19_vai_1, main_20_vai_1,
       main_21_vai_1, main_22_vai_1, main_23_vai_1, main_24_vai_1, main_26_vai_1, main_27_vai_1,
       main_28_vai_1, main_29_vai_1, main_30_vai_1, main_31_vai_1, main_32_vai_1, overflow_fora_1_out_4;

  and and_1 (and_1_out, ~in_2[4], ~in_2[3], in_2[2], ~in_2[1], ~in_2[0]);  // AND_Gate
  Overflow_Fora overflow_fora_1 (.A(A[31]), .B(B[31]), .S(B[0]), .out_4(overflow_fora_1_out_4));
  main main_1 (.vem_1(main_5_vai_1), .A(A[31]), .B(B[31]), .in_4(in_2), .S(S[28]), .Vai_1(main_1_vai_1));
  main main_2 (.vem_1(main_6_vai_1), .A(A[30]), .B(B[30]), .in_4(in_2), .S(S[29]), .Vai_1(main_2_vai_1));
  main main_3 (.vem_1(main_7_vai_1), .A(A[29]), .B(B[29]), .in_4(in_2), .S(S[30]), .Vai_1(main_3_vai_1));
  main main_4 (.vem_1(main_8_vai_1), .A(A[28]), .B(B[28]), .in_4(in_2), .S(S[31]), .Vai_1(main_4_vai_1));
  main main_5 (.vem_1(main_9_vai_1), .A(A[27]), .B(B[27]), .in_4(in_2), .S(S[24]), .Vai_1(main_5_vai_1));
  main main_6 (.vem_1(main_10_vai_1), .A(A[26]), .B(B[26]), .in_4(in_2), .S(S[25]), .Vai_1(main_6_vai_1));
  main main_7 (.vem_1(main_11_vai_1), .A(A[25]), .B(B[25]), .in_4(in_2), .S(S[26]), .Vai_1(main_7_vai_1));
  main main_8 (.vem_1(main_12_vai_1), .A(A[24]), .B(B[24]), .in_4(in_2), .S(S[27]), .Vai_1(main_8_vai_1));
  Multiplexer #(.enable("false")) multiplexer_1 (
    .in0(overflow_fora_1_out_4), .in1(main_5_vai_1), .out(out_5), .sel(and_1_out));
  main main_9 (.vem_1(main_13_vai_1), .A(A[23]), .B(B[20]), .in_4(in_2), .S(S[20]), .Vai_1(main_9_vai_1));
  main main_10 (.vem_1(main_14_vai_1), .A(A[22]), .B(B[21]), .in_4(in_2), .S(S[21]), .Vai_1(main_10_vai_1));
  main main_11 (.vem_1(main_15_vai_1), .A(A[21]), .B(B[22]), .in_4(in_2), .S(S[22]), .Vai_1(main_11_vai_1));
  main main_12 (.vem_1(S[19]), .A(A[20]), .B(B[23]), .in_4(in_2), .S(S[23]), .Vai_1(main_12_vai_1));
  main main_13 (.vem_1(main_17_vai_1), .A(A[19]), .B(B[19]), .in_4(in_2), .S(S[16]), .Vai_1(main_13_vai_1));
  main main_14 (.vem_1(main_18_vai_1), .A(A[18]), .B(B[18]), .in_4(in_2), .S(S[17]), .Vai_1(main_14_vai_1));
  main main_15 (.vem_1(main_19_vai_1), .A(A[17]), .B(B[17]), .in_4(in_2), .S(S[18]), .Vai_1(main_15_vai_1));
  main main_16 (.vem_1(main_20_vai_1), .A(A[16]), .B(B[16]), .in_4(in_2), .S(S[19]), .Vai_1(S[19]));
  main main_17 (.vem_1(main_21_vai_1), .A(A[15]), .B(B[15]), .in_4(in_2), .S(S[12]), .Vai_1(main_17_vai_1));
  main main_18 (.vem_1(main_22_vai_1), .A(A[14]), .B(B[14]), .in_4(in_2), .S(S[13]), .Vai_1(main_18_vai_1));
  main main_19 (.vem_1(main_23_vai_1), .A(A[13]), .B(B[13]), .in_4(in_2), .S(S[14]), .Vai_1(main_19_vai_1));
  main main_20 (.vem_1(main_24_vai_1), .A(A[12]), .B(B[12]), .in_4(in_2), .S(S[15]), .Vai_1(main_20_vai_1));
  main main_21 (.vem_1(S[4]), .A(A[11]), .B(B[11]), .in_4(in_2), .S(S[8]), .Vai_1(main_21_vai_1));
  main main_22 (.vem_1(main_26_vai_1), .A(A[10]), .B(B[10]), .in_4(in_2), .S(S[9]), .Vai_1(main_22_vai_1));
  main main_23 (.vem_1(main_27_vai_1), .A(A[9]), .B(B[9]), .in_4(in_2), .S(S[10]), .Vai_1(main_23_vai_1));
  main main_24 (.vem_1(main_28_vai_1), .A(A[8]), .B(B[8]), .in_4(in_2), .S(S[11]), .Vai_1(main_24_vai_1));
  main main_25 (.vem_1(main_29_vai_1), .A(A[7]), .B(B[7]), .in_4(in_2), .S(S[4]), .Vai_1(S[4]));
  main main_26 (.vem_1(main_30_vai_1), .A(A[6]), .B(B[6]), .in_4(in_2), .S(S[5]), .Vai_1(main_26_vai_1));
  main main_27 (.vem_1(main_31_vai_1), .A(A[5]), .B(B[5]), .in_4(in_2), .S(S[6]), .Vai_1(main_27_vai_1));
  main main_28 (.vem_1(main_32_vai_1), .A(A[4]), .B(B[4]), .in_4(in_2), .S(S[7]), .Vai_1(main_28_vai_1));
  main main_29 (.A(A[3]), .B(B[0]), .in_4(in_2), .S(B[0]), .Vai_1(main_29_vai_1));  // open: vem_1
  main main_30 (.vem_1(main_2_vai_1), .A(A[2]), .B(B[3]), .in_4(in_2), .S(S[1]), .Vai_1(main_30_vai_1));
  main main_31 (.vem_1(main_3_vai_1), .A(A[1]), .B(B[2]), .in_4(in_2), .S(S[2]), .Vai_1(main_31_vai_1));
  main main_32 (.vem_1(main_4_vai_1), .A(A[0]), .B(B[1]), .in_4(in_2), .S(S[3]), .Vai_1(main_32_vai_1));
  and and_2 (Zero, ~S[31], ~S[30], ~S[29], ~S[28], ~S[27], ~S[26], ~S[25], ~S[24], ~S[23], ~S[22], ~S[21], ~S[20], ~S[19], ~S[18], ~S[17], S[16], ~S[15], ~S[14], ~S[13], ~S[12], ~S[11], ~S[10], ~S[9], ~S[8], ~S[7], ~S[6], ~S[5], ~S[4], ~S[3], ~S[2], ~S[1], ~B[0]);  // AND_Gate

  assign S[0] = B[0];
endmodule

module Overflow (
  input  A,
  input  B,
  input  S,
  input  Vem_1,
  input  [4:0] entrada,
  output S1
);

  wire and_1_out, and_2_out, or_1_out;

  and and_1 (and_1_out, ~A, S, ~B);  // AND_Gate
  and and_2 (and_2_out, A, ~S, B);  // AND_Gate
  or or_1 (or_1_out, and_1_out, and_2_out);
  Multiplexer #(.select(5), .enable("false")) multiplexer_1 (
    .in0(or_1_out), .in1(Vem_1), .out(S1), .sel(entrada));  // open: in2, in3, in4, in5, in6, in7, in8, in9, in10, in11, in12, in13, in14, in15, in16, in17, in18, in19, in20, in21, in22, in23, in24, in25, in26, in27, in28, in29, in30, in31
endmodule

module Overflow_Fora (
  input  A,
  input  B,
  input  S,
  output out_4
);

  wire and_1_out, and_2_out;

  and and_1 (and_1_out, ~A, S, ~B);  // AND_Gate
  and and_2 (and_2_out, A, ~S, B);  // AND_Gate
  or or_1 (out_4, and_1_out, and_2_out);
endmodule
