// Logisim project celula S ULA.circ as structural Verilog: 4 circuits, main circuit main
module main (
  input  Esquerda,
  input  Direita,
  input  A,
  input  B,
  input  [4:0] in_5,
  input  Vem_1,
  output out_7,
  output Vaik_1
);

  wire adder_1_cout, adder_1_out, and_1_out, and_2_out, nand_1_out, or_1_out, subtractor_1_bout,
       subtractor_1_out, xor_1_out;

  and and_1 (and_1_out, A, B);
  or or_1 (or_1_out, A, B);
  nand nand_1 (nand_1_out, A, B);
  xor xor_1 (xor_1_out, A, B);
  Adder #(.width(1)) adder_1 (.a(A), .b(B), .out(adder_1_out), .cin(Vem_1), .cout(adder_1_cout));
  Subtractor #(.width(1)) subtractor_1 (.a(B), .b(A), .out(subtractor_1_out), .bin(Vem_1), .bout(subtractor_1_bout));
  and and_2 (and_2_out, ~in_5[4], ~in_5[3], in_5[2], in_5[1], ~in_5[0]);  // AND_Gate
  Multiplexer #(.enable("false")) multiplexer_1 (
    .in0(adder_1_cout), .in1(subtractor_1_bout), .out(Vaik_1), .sel(and_2_out));
  Multiplexer #(.select(5), .enable("false")) multiplexer_2 (
    .in0(and_1_out), .in1(or_1_out), .in2(nand_1_out), .in3(xor_1_out), .in4(adder_1_out),
    .in5(subtractor_1_out), .in6(Direita), .in7(Direita), .in8(Esquerda), .out(out_7), .sel(in_5));  // open: in9, in10, in11, in12, in13, in14, in15, in16, in17, in18, in19, in20, in21, in22, in23, in24, in25, in26, in27, in28, in29, in30, in31
endmodule

module ULA (
  input  [7:0] A,
  input  [4:0] Seletor,
  input  [7:0] B,
  output [7:0] S,
  output out_5
);

  wire main_1_vaik_1, main_2_vaik_1, main_3_vaik_1, main_4_vaik_1, main_5_vaik_1, main_6_vaik_1,
       main_7_vaik_1;

  celula_S celula_s_1 (
    .Esquerda(A[6]), .A(A[7]), .B(B[7]), .Vem_1(main_1_vaik_1), .in_5(Seletor), .direita_aritimetica(A[7]),
    .Direita(1'b0), .out_8(S[7]), .Vai_1(out_5));
  main main_1 (
    .Esquerda(A[5]), .A(A[6]), .B(B[6]), .Vem_1(main_2_vaik_1), .in_5(Seletor), .Direita(A[7]), .out_7(S[6]),
    .Vaik_1(main_1_vaik_1));
  main main_2 (
    .Esquerda(A[4]), .A(A[5]), .B(B[5]), .Vem_1(main_3_vaik_1), .in_5(Seletor), .Direita(A[6]), .out_7(S[5]),
    .Vaik_1(main_2_vaik_1));
  main main_3 (
    .Esquerda(A[3]), .A(A[4]), .B(B[4]), .Vem_1(main_4_vaik_1), .in_5(Seletor), .Direita(A[5]), .out_7(S[4]),
    .Vaik_1(main_3_vaik_1));
  main main_4 (
    .Esquerda(A[2]), .A(A[3]), .B(B[3]), .Vem_1(main_5_vaik_1), .in_5(Seletor), .Direita(A[4]), .out_7(S[3]),
    .Vaik_1(main_4_vaik_1));
  main main_5 (
    .Esquerda(A[1]), .A(A[2]), .B(B[2]), .Vem_1(main_6_vaik_1), .in_5(Seletor), .Direita(A[3]), .out_7(S[2]),
    .Vaik_1(main_5_vaik_1));
  main main_6 (
    .A(A[1]), .B(B[1]), .Vem_1(main_7_vaik_1), .in_5(Seletor), .Direita(A[2]), .out_7(S[1]),
    .Vaik_1(main_6_vaik_1));  // open: Esquerda
  main main_7 (
    .Esquerda(1'b0), .A(A[0]), .B(B[0]), .Vem_1(1'b0), .in_5(Seletor), .Direita(A[1]), .out_7(S[0]),
    .Vaik_1(main_7_vaik_1));
endmodule

module celula_S (
  input  Esquerda,
  input  Direita,
  input  A,
  input  B,
  input  [4:0] in_5,
  input  Vem_1,
  input  direita_aritimetica,
  output out_8,
  output Vai_1
);

  wire adder_1_cout, adder_1_out, and_1_out, and_2_out, nand_1_out, or_1_out, subtractor_1_bout,
       subtractor_1_out, xor_1_out;

  and and_1 (and_1_out, A, B);
  or or_1 (or_1_out, A, B);
  nand nand_1 (nand_1_out, A, B);
  xor xor_1 (xor_1_out, A, B);
  Adder #(.width(1)) adder_1 (.a(A), .b(B), .out(adder_1_out), .cin(Vem_1), .cout(adder_1_cout));
  Subtractor #(.width(1)) subtractor_1 (.a(B), .b(A), .out(subtractor_1_out), .bin(Vem_1), .bout(subtractor_1_bout));
  and and_2 (and_2_out, ~in_5[4], ~in_5[3], in_5[2], in_5[1], ~in_5[0]);  // AND_Gate
  Multiplexer #(.enable("false")) multiplexer_1 (
    .in0(adder_1_cout), .in1(subtractor_1_bout), .out(Vai_1), .sel(and_2_out));
  Multiplexer #(.select(5), .enable("false")) multiplexer_2 (
    .in0(and_1_out), .in1(or_1_out), .in2(nand_1_out), .in3(xor_1_out), .in4(adder_1_out),
    .in5(subtractor_1_out), .in6(Direita), .in7(Direita), .in8(direita_aritimetica), .in9(Esquerda),
    .out(out_8), .sel(in_5));  // open: in10, in11, in12, in13, in14, in15, in16, in17, in18, in19, in20, in21, in22, in23, in24, in25, in26, in27, in28, in29, in30, in31
endmodule

module Overflow (
);

  // AND_Gate and_1 is placed but not wired
  // AND_Gate and_2 is placed but not wired
endmodule
