// Logisim project celula ULA.circ as structural Verilog
module main (
  input  Esquerda,
  input  Direita,
  input  A,
  input  B,
  input  [4:0] in_5,
  input  Vem_1,
  input  Vai_1,
  output out_8
);

  wire adder_1_cout, adder_1_out, and_1_out, and_2_out, nand_1_out, or_1_out, subtractor_1_bout,
       subtractor_1_out, xor_1_out;

  and and_1 (and_1_out, A, B);
  or or_1 (or_1_out, A, B);
  nand nand_1 (nand_1_out, A, B);
  xor xor_1 (xor_1_out, A, B);
  Adder #(.width(1)) adder_1 (.a(A), .b(B), .out(adder_1_out), .cin(Vem_1), .cout(adder_1_cout));
  Subtractor #(.width(1)) subtractor_1 (.a(B), .b(A), .out(subtractor_1_out), .bin(Vem_1), .bout(subtractor_1_bout));
  and and_2 (and_2_out, ~in_5[4], ~in_5[3], in_5[2], in_5[1], ~in_5[0]);  // AND_Gate
  Multiplexer #(.enable("false")) multiplexer_1 (
    .in0(adder_1_cout), .in1(subtractor_1_bout), .out(Vai_1), .sel(and_2_out));
  Multiplexer #(.select(5), .enable("false")) multiplexer_2 (
    .in0(and_1_out), .in1(or_1_out), .in2(nand_1_out), .in3(xor_1_out), .in4(adder_1_out),
    .in5(subtractor_1_out), .in6(Direita), .in7(Direita), .in8(Esquerda), .out(out_8), .sel(in_5));  // open: in9, in10, in11, in12, in13, in14, in15, in16, in17, in18, in19, in20, in21, in22, in23, in24, in25, in26, in27, in28, in29, in30, in31
endmodule

module celula_S (
  input  Esquerda,
  input  Direita,
  input  A,
  input  B,
  input  [4:0] in_5,
  input  Vem_1,
  input  Vai_1,
  input  direita_aritimetica,
  output out_9
);

  wire adder_1_cout, adder_1_out, and_1_out, and_2_out, nand_1_out, or_1_out, subtractor_1_bout,
       subtractor_1_out, xor_1_out;

  and and_1 (and_1_out, A, B);
  or or_1 (or_1_out, A, B);
  nand nand_1 (nand_1_out, A, B);
  xor xor_1 (xor_1_out, A, B);
  Adder #(.width(1)) adder_1 (.a(A), .b(B), .out(adder_1_out), .cin(Vem_1), .cout(adder_1_cout));
  Subtractor #(.width(1)) subtractor_1 (.a(B), .b(A), .out(subtractor_1_out), .bin(Vem_1), .bout(subtractor_1_bout));
  and and_2 (and_2_out, ~in_5[4], ~in_5[3], in_5[2], in_5[1], ~in_5[0]);  // AND_Gate
  Multiplexer #(.enable("false")) multiplexer_1 (
    .in0(adder_1_cout), .in1(subtractor_1_bout), .out(Vai_1), .sel(and_2_out));
  Multiplexer #(.select(5), .enable("false")) multiplexer_2 (
    .in0(and_1_out), .in1(or_1_out), .in2(nand_1_out), .in3(xor_1_out), .in4(adder_1_out),
    .in5(subtractor_1_out), .in6(Direita), .in7(Direita), .in8(direita_aritimetica), .in9(Esquerda),
    .out(out_9), .sel(in_5));  // open: in10, in11, in12, in13, in14, in15, in16, in17, in18, in19, in20, in21, in22, in23, in24, in25, in26, in27, in28, in29, in30, in31
endmodule
