// Digital circuit flip-Flop JK Mestre-escravo.dig as structural Verilog
module flip_Flop_JK_Mestre_escravo (
  input  in_1,
  input  clk,
  input  in_3,
  input  clk_2,
  input  in_5,
  input  in_6,
  output out_7,
  output out_8
);

  wire nand_1_out, nand_2_out, nand_3_out, nand_4_out, nand_5_out, not_1_out, xnor_1_out;

  nand nand_1 (nand_1_out, in_1, clk, nand_3_out);
  xnor xnor_1 (xnor_1_out, nand_2_out, clk, in_3);
  nand nand_2 (nand_2_out, in_5, nand_1_out, nand_3_out);
  nand nand_3 (nand_3_out, nand_2_out, xnor_1_out, in_6);
  not not_1 (not_1_out, clk_2);
  nand nand_4 (nand_4_out, nand_2_out, not_1_out);
  nand nand_5 (nand_5_out, not_1_out, nand_3_out);
  nand nand_6 (out_7, in_5, nand_4_out, out_8);
  nand nand_7 (out_8, out_7, nand_5_out, in_6);
endmodule
